# Fritzing sketch i-gauge LoRa Gateway (saved by Fritzing 0.9.3b)
circuit board: 15cm x 5.64cm

parts:
  Part2 = Logic Level Converter
  LoRa = Adafruit RFM9x LoRa Radio [part_number="Adafruit #3072 and #3073"]
  WeMos_D1_Mini_Micro_SD_&_RTC_Shield = WeMos D1 Mini Micro SD Shield [part_number="WeMos DataLogger Shield"]
  GSM_-_SIM800L = SIM800L [package=THT]
  LED1 = RGB LED (com. cathode, rgb) [package="5 mm [THT]"]
  R1 = Resistor [tolerance=±5% resistance=220 package=THT]
  R2 = Resistor [tolerance=±5% resistance=220 package=THT]
  R3 = Resistor [tolerance=±5% resistance=220 package=THT]
  Part5 = Logic Level Converter
  ARDUINO_MEGA = Arduino Mega 2560 (Rev3)
  Part7 = Adafruit RGB LCD Shield [part_number="Adafruit #714 and #716"]

nets:
  N1: Part2.TX2_LV, LoRa.MISO, WeMos_D1_Mini_Micro_SD_&_RTC_Shield.D6
  N2: Part2.RX2_LV, LoRa.MOSI, WeMos_D1_Mini_Micro_SD_&_RTC_Shield.D7
  GND: Part2.GND, LoRa.GND, WeMos_D1_Mini_Micro_SD_&_RTC_Shield.G, GSM_-_SIM800L.GND, LED1.common_cathode, Part5.GND, ARDUINO_MEGA.GND, Part7.GND
  3V3: Part2.LV, LoRa.VIN, WeMos_D1_Mini_Micro_SD_&_RTC_Shield.3V3, Part5.LV, ARDUINO_MEGA.3V3
  N3: Part2.RX_LV, LoRa.SCK, WeMos_D1_Mini_Micro_SD_&_RTC_Shield.D5
  N4: Part2.TX_LV, LoRa.CS
  N5: Part2.TX_HV, ARDUINO_MEGA.D53
  N6: Part2.RX_HV, ARDUINO_MEGA.D52
  5V: Part2.HV, WeMos_D1_Mini_Micro_SD_&_RTC_Shield.5V, GSM_-_SIM800L.5V, Part5.HV, ARDUINO_MEGA.5V, Part7.+5V
  N7: Part2.RX2_HV, ARDUINO_MEGA.D51
  N8: Part2.TX2_HV, ARDUINO_MEGA.D50
  N9: LoRa.DIO0, ARDUINO_MEGA.D3_PWM
  N10: LoRa.RST, ARDUINO_MEGA.D7_PWM
  N11: WeMos_D1_Mini_Micro_SD_&_RTC_Shield.D1, ARDUINO_MEGA.D21/SCL, ARDUINO_MEGA.SCL, Part7.SCL
  N12: WeMos_D1_Mini_Micro_SD_&_RTC_Shield.D2, ARDUINO_MEGA.D20/SDA, Part7.SDA
  N13: WeMos_D1_Mini_Micro_SD_&_RTC_Shield.D8, Part5.TX_LV
  N14: GSM_-_SIM800L.SIM_TXD, ARDUINO_MEGA.D19/RX1
  N15: GSM_-_SIM800L.SIM_RXD, ARDUINO_MEGA.D18/TX1
  N16: LED1.red_anode, R1.Pin_0
  N17: LED1.green_anode, R2.Pin_0
  N18: LED1.blue_anode, R3.Pin_0
  N19: R1.Pin_1, ARDUINO_MEGA.D34
  N20: R2.Pin_1, ARDUINO_MEGA.D36
  N21: R3.Pin_1, ARDUINO_MEGA.D38
  N22: Part5.TX_HV, ARDUINO_MEGA.D10_PWM

custom parts:
  Adafruit RFM9x LoRa Radio: Sending data over long distances is like magic, and now you can be a magician with this range of powerful and easy-to-use radio modules. Sure, sometimes you want to talk to a computer (a good time to use WiFi) or perhaps communicate with a Phone (choose Bluetooth Low Energy!) but what if you want to send data very far? Most WiFi, Bluetooth, Zigbee and other wireless chipsets use 2.4GHz, which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
  Adafruit RGB LCD Shield: This new Adafruit shield makes it easy to use a 16x2 Character LCD. We really like the RGB LCDs we stock in the shop both the RGB negative and RGB positive. Unfortunately, these LCDs do require quite a few digital pins, 6 to control the LCD and then another 3 to control the RGB backlight for a total of 9 pins. That's half of the pins available on a classic Arduino! With this in mind, we wanted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
